# Fritzing sketch Circuit (saved by Fritzing 0.9.4)
breadboards: 1

parts:
  Mod1 = Raspberry Pi 4B
  S1 = Round Pushbutton
  S2 = Round Pushbutton
  M1 = fc-51 [package=THT]
  J1 = Basic Servo
  Mod2 = KY-016 RGB Full Color LED Module [package="Breakout board"]

nets:
  5V: Mod1.5V, M1.pin3, J1.vcc
  GND: Mod1.GND, S1.leg1, S2.leg1, M1.pin2, J1.gnd, Mod2.-
  N1: Mod1.GPIO4, J1.pulse
  N2: Mod1.GPIO27, S1.leg0
  N3: Mod1.GPIO22, M1.pin1
  N4: Mod1.GPIO5, Mod2.B
  N5: Mod1.GPIO6, Mod2.G
  N6: Mod1.GPIO19, Mod2.R

notes:
  CONNECTED TO RASPBERRY PI HEADER
  Start Stop
  CONNECTED TO RASPBERRY VIA RIBBION CABLE

custom parts:
  KY-016 RGB Full Color LED Module: KY-016 Arduino full color 5mm RGB LED, different colors can be obtained by mixing the three primary colors.
